# Fritzing sketch Lichterkette (saved by Fritzing 0.9.9b)
circuit board: 8.547cm x 5.02352cm
breadboards: 1

parts:
  C1 = Electrolytic Capacitor [capacitance=100µF voltage=35V package="100 mil [THT, electrolytic]"]
  LED_1 = screw terminal, 3 pins
  R1 = Resistor [tolerance=±5% power=0.25 resistance=470 package=THT]
  U3 = 74AHCT125 [part_number=SN74AHCT125 package=dil14]
  LED_2 = screw terminal, 3 pins
  LED_3 = screw terminal, 3 pins
  LED_4 = screw terminal, 3 pins
  R3 = Resistor [tolerance=±5% power=0.25 resistance=470 package=THT]
  R2 = Resistor [tolerance=±5% power=0.25 resistance=470 package=THT]
  R4 = Resistor [tolerance=±5% power=0.25 resistance=470 package=THT]
  J1 = Screw terminal - 2 pins [package=THT]
  MH-ET_LIVE_ESP32_DEVKIT1 = MH-ET LIVE ESP32 DEVKIT 38 pins

nets:
  N1: C1.-, LED_1.pin3, U3.1OE, U3.2OE, U3.GND, U3.3A, U3.4A, LED_2.pin3, LED_3.pin3, LED_4.pin3, J1.pin2, MH-ET_LIVE_ESP32_DEVKIT1.GND#58
  VCC: C1.+, LED_1.pin1, U3.VCC, LED_2.pin1, LED_3.pin1, LED_4.pin1, J1.pin1, MH-ET_LIVE_ESP32_DEVKIT1.5V
  N2: LED_1.pin2, R1.Pin_1
  N3: R1.Pin_0, U3.1Y
  N4: U3.1A, MH-ET_LIVE_ESP32_DEVKIT1.IO2
  N5: U3.2A, MH-ET_LIVE_ESP32_DEVKIT1.IO0
  N6: U3.2Y, R2.Pin_0
  N7: U3.3Y, R3.Pin_0
  N8: U3.3OE, MH-ET_LIVE_ESP32_DEVKIT1.IO4
  N9: U3.4Y, R4.Pin_0
  N10: U3.4OE, MH-ET_LIVE_ESP32_DEVKIT1.IO15
  N11: LED_2.pin2, R2.Pin_1
  N12: LED_3.pin2, R3.Pin_1
  N13: LED_4.pin2, R4.Pin_1

notes:
  Regenbogenreich LED Controller
  Version 0.1
  Eric, Eva und der Papsi

custom parts:
  74AHCT125: Quad Level-Shifter (3V to 5V) Quadruple Bus Buffer Gates With 3-State Outputs
  MH-ET LIVE ESP32 DEVKIT 38 pins: http://mh.nodebb.com/topic/2/mh-et-live-esp32-devkit
