# Fritzing sketch Lichterkette_backup (saved by Fritzing 0.9.9b)
circuit board: 7.56903cm x 5.21407cm
breadboards: 1

parts:
  Mod1 = Heltec WiFi LoRa 32 V2 [part_number=HTIT-WB32LA]
  U1 = SN74LS32N [package="DIP14 [THT]"]
  R1 = Resistor [tolerance=±5% power=0.25 resistance=470 package=THT]
  C1 = Electrolytic Capacitor [capacitance=100µF voltage=35V package="100 mil [THT, electrolytic]"]
  Power_plug1 = Power plug
  U2 = WS2812 RGB LED strip
  J1 = female pin header, 2 pins [form="♀ (female)"]  # not connected
  J2 = Camdenboss CTB0158-2 [part_number=CTB0158-2 package=THT]  # not connected
  S1 = Pushbutton [package=THT]  # not connected
  J3 = JST-03JQ-BT [part_number=JST-JQ-BT package=THT]  # not connected

nets:
  N1: Mod1.pin_16, Mod1.pin_17
  GND: Mod1.GND, U1.1A, U1.GND, C1.-, Power_plug1.GND, U2.GND
  VCC: Mod1.pin_20, U1.Vcc, C1.+, Power_plug1.VCC, U2.VCC
  N2: Mod1.pin_21, Mod1.pin_22
  N3: Mod1.pin_29, U1.1B
  N4: U1.1Y, R1.Pin_0
  N5: R1.Pin_1, U2.DIN

notes:
  Regenbogenreich LED Controller V0.1

custom parts:
  WS2812 RGB LED strip: WS2812 strip
